// Logisim project regfile.circ as structural Verilog: 1 circuit, main circuit main
module main (
  input  [4:0] Read_Register_1,
  input  [4:0] Read_Register_2,
  input  [4:0] Write_Register,
  input  [31:0] Write_Data,
  input  Write_Enable,
  input  Clock,
  input  [31:0] R15,
  output [31:0] R0_Value,
  output [31:0] R1_Value,
  output [31:0] R3_Value,
  output [31:0] LR__R14__Value,
  output [31:0] SP__R13__Value,
  output [31:0] Read_Data_1,
  output [31:0] Read_Data_2
);

  wire comparator_1_eq, comparator_2_eq, registerfile_1_p1, registerfile_1_p2, registerfile_1_p4,
       registerfile_1_p6, registerfile_2_p1, registerfile_2_p4, registerfile_2_p8, registerfile_2_p14,
       registerfile_2_p16, registerfile_4_p6;
  wire [31:0] R15Value, registerfile_2_p12, registerfile_2_p13;

  Register #(.width(32)) register_1 (.D(R15), .Q(R15Value), .clk(Clock));  // open: en, clr
  // RegisterFile registerfile_1: pin names not known; wires that end beside it: registerfile_1_p1, registerfile_1_p2, registerfile_1_p2, registerfile_1_p4, registerfile_1_p4, registerfile_1_p6, Write_Data, Clock, Write_Enable, Write_Register, 5'b01101, 5'b01110, SP__R13__Value, LR__R14__Value
  // RegisterFile registerfile_2: pin names not known; wires that end beside it: registerfile_2_p1, Write_Data, Clock, registerfile_2_p4, Write_Enable, registerfile_2_p4, Write_Register, registerfile_2_p8, Read_Register_1, Read_Register_2, registerfile_2_p8, registerfile_2_p12, registerfile_2_p13, registerfile_2_p14, registerfile_2_p14, registerfile_2_p16, registerfile_2_p16, registerfile_2_p1
  Comparator #(.width(5)) comparator_1 (.a(5'b01111), .b(Read_Register_1), .eq(comparator_1_eq));  // open: gt, lt
  // RegisterFile registerfile_3: pin names not known; wires that end beside it: Write_Data, Clock, Write_Enable, Write_Register, {5{1'b0}}, 5'b00001, R0_Value, R1_Value
  Multiplexer #(.width(32), .enable("false")) multiplexer_1 (
    .in0(registerfile_2_p12), .in1(R15Value), .out(Read_Data_1), .sel(comparator_1_eq));
  Multiplexer #(.width(32), .enable("false")) multiplexer_2 (
    .in0(registerfile_2_p13), .in1(R15Value), .out(Read_Data_2), .sel(comparator_2_eq));
  Comparator #(.width(5)) comparator_2 (.a(5'b01111), .b(Read_Register_2), .eq(comparator_2_eq));  // open: gt, lt
  // RegisterFile registerfile_4: pin names not known; wires that end beside it: Write_Data, Clock, Write_Enable, Write_Register, 5'b00010, registerfile_4_p6, registerfile_4_p6, R3_Value

  // Other names for the same wires on the sheet: clk = Clock; lr[31:0] = LR__R14__Value; r0[31:0] = R0_Value;
  //   r1[31:0] = R1_Value; r2[31:0] = R3_Value; read_reg1[4:0] = Read_Register_1; read_reg2[4:0] = Read_Register_2;
  //   sp[31:0] = SP__R13__Value; write_en = Write_Enable; write_reg[4:0] = Write_Register

  // Notes on the sheet:
  //   INPUTS to your circuit
  //   DON'T CHANGE THE LOCATIONS OF THE INPUTS AND OUTPUTS!
  //   PC+8 (R15) really lives here
  //   These are DEBUG/TEST outputs from your circuit.
  //   copies
  //   OUTPUTS from your circuit
endmodule
